// Logisim project maint.circ as structural Verilog: 7 circuits, main circuit main
module main (
  input  on,
  input  bus_0,
  input  bus_0_2,
  input  [31:0] bus_0_3
);

  wire cdm_8_mark5_1_p4, cdm_8_mark5_1_p5, cdm_8_mark5_1_p7, cdm_8_mark5_1_p8, clock, code,
       cursor_1_is_enter, data, I_Osel, IAck, In_out, IRQ, mem, nand_1_out, not_1_out, not_2_out, RAM;
  wire [2:0] vec;
  wire [4:0] cursor_1_x, cursor_1_y;
  wire [6:0] keyboard_1_data;
  wire [7:0] cdm_8_mark5_1_p12, cdm_8_mark5_1_p13, I_Oadr, I_Odata;
  wire [31:0] converter_1_converted_row, cursor_visualization_1_row_0_2, cursor_visualization_1_row_1_2,
       cursor_visualization_1_row_2_2, cursor_visualization_1_row_3_2, cursor_visualization_1_row_4_2,
       cursor_visualization_1_row_5_2, cursor_visualization_1_row_6_2, cursor_visualization_1_row_7_2,
       cursor_visualization_1_row_8_2, cursor_visualization_1_row_9_2, cursor_visualization_1_row_10_2,
       cursor_visualization_1_row_11_2, cursor_visualization_1_row_12_2, cursor_visualization_1_row_13_2,
       cursor_visualization_1_row_14_2, cursor_visualization_1_row_15_2, cursor_visualization_1_row_16_2,
       cursor_visualization_1_row_17_2, cursor_visualization_1_row_18_2, cursor_visualization_1_row_19_2,
       cursor_visualization_1_row_20_2, cursor_visualization_1_row_21_2, cursor_visualization_1_row_22_2,
       cursor_visualization_1_row_23_2, cursor_visualization_1_row_24_2, cursor_visualization_1_row_25_2,
       cursor_visualization_1_row_26_2, cursor_visualization_1_row_27_2, cursor_visualization_1_row_28_2,
       cursor_visualization_1_row_29_2, cursor_visualization_1_row_30_2, cursor_visualization_1_row_31_2,
       fixed_buffer_1_row_0_2, fixed_buffer_1_row_1_2, fixed_buffer_1_row_2_2, fixed_buffer_1_row_3_2,
       fixed_buffer_1_row_4_2, fixed_buffer_1_row_5_2, fixed_buffer_1_row_6_2, fixed_buffer_1_row_7_2,
       fixed_buffer_1_row_8_2, fixed_buffer_1_row_9_2, fixed_buffer_1_row_10_2, fixed_buffer_1_row_11_2,
       fixed_buffer_1_row_12_2, fixed_buffer_1_row_13_2, fixed_buffer_1_row_14_2, fixed_buffer_1_row_15_2,
       fixed_buffer_1_row_16_2, fixed_buffer_1_row_17_2, fixed_buffer_1_row_18_2, fixed_buffer_1_row_19_2,
       fixed_buffer_1_row_20_2, fixed_buffer_1_row_21_2, fixed_buffer_1_row_22_2, fixed_buffer_1_row_23_2,
       fixed_buffer_1_row_24_2, fixed_buffer_1_row_25_2, fixed_buffer_1_row_26_2, fixed_buffer_1_row_27_2,
       fixed_buffer_1_row_28_2, fixed_buffer_1_row_29_2, fixed_buffer_1_row_30_2, fixed_buffer_1_row_31_2,
       write_buffer_1_row0, write_buffer_1_row0_2, write_buffer_1_row0_3, write_buffer_1_row0_4,
       write_buffer_1_row0_5, write_buffer_1_row0_6, write_buffer_1_row0_7, write_buffer_1_row0_8,
       write_buffer_1_row0_9, write_buffer_1_row0_10, write_buffer_1_row0_11, write_buffer_1_row0_12,
       write_buffer_1_row0_13, write_buffer_1_row0_14, write_buffer_1_row0_15, write_buffer_1_row0_16,
       write_buffer_1_row0_17, write_buffer_1_row1, write_buffer_1_row2, write_buffer_1_row3,
       write_buffer_1_row4, write_buffer_1_row5, write_buffer_1_row6, write_buffer_1_row7,
       write_buffer_1_row8, write_buffer_1_row9, write_buffer_1_row10, write_buffer_1_row11,
       write_buffer_1_row12, write_buffer_1_row13, write_buffer_1_row14, write_buffer_1_row15;

  and and_1 (I_Osel, not_1_out, clock, data);
  Keyboard keyboard_1 (.clk(clock), .data(keyboard_1_data));  // open: re, clr, avail
  // Probe on cdm_8_mark5_1_p4
  // Probe on cdm_8_mark5_1_p5
  // Probe on cdm_8_mark5_1_p7
  // Probe on nothing
  Clock clock_1 (.out(clock));
  not not_1 (not_1_out, nand_1_out);
  and and_2 (RAM, nand_1_out, data);
  // CdM_8_mark5 cdm_8_mark5_1: pin names not known; wires that end beside it: IRQ, vec, IAck, cdm_8_mark5_1_p4, cdm_8_mark5_1_p5, clock, cdm_8_mark5_1_p7, cdm_8_mark5_1_p8, mem, In_out, I_Oadr, cdm_8_mark5_1_p12, cdm_8_mark5_1_p13
  assign cdm_8_mark5_1_p13 = In_out ? I_Odata : 8'bz;  // Controlled_Buffer controlled_buffer_1
  nand nand_1 (nand_1_out, I_Oadr[4], I_Oadr[5], I_Oadr[6], I_Oadr[7]);
  cursor cursor_1 (.ASCII_code(keyboard_1_data), .X(cursor_1_x), .Y(cursor_1_y), .is_enter(cursor_1_is_enter));
  write_buffer write_buffer_1 (
    .clear(bus_0), .write_not(cursor_1_is_enter), .row(cursor_1_y), .row0(write_buffer_1_row0),
    .row1(write_buffer_1_row1), .row2(write_buffer_1_row2), .row3(write_buffer_1_row3),
    .row4(write_buffer_1_row4), .row5(write_buffer_1_row5), .row6(write_buffer_1_row6),
    .row7(write_buffer_1_row7), .row8(write_buffer_1_row8), .row9(write_buffer_1_row9),
    .row10(write_buffer_1_row10), .row11(write_buffer_1_row11), .row12(write_buffer_1_row12),
    .row13(write_buffer_1_row13), .row14(write_buffer_1_row14), .row15(write_buffer_1_row15),
    .row0_2(write_buffer_1_row0_2), .row0_3(write_buffer_1_row0_3), .row0_4(write_buffer_1_row0_4),
    .row0_5(write_buffer_1_row0_5), .row0_6(write_buffer_1_row0_6), .row0_7(write_buffer_1_row0_7),
    .row0_8(write_buffer_1_row0_8), .row0_9(write_buffer_1_row0_9), .row0_10(write_buffer_1_row0_10),
    .row0_11(write_buffer_1_row0_11), .row0_12(write_buffer_1_row0_12), .row0_13(write_buffer_1_row0_13),
    .row0_14(write_buffer_1_row0_14), .row0_15(write_buffer_1_row0_15), .row0_16(write_buffer_1_row0_16),
    .row0_17(write_buffer_1_row0_17), .\input (converter_1_converted_row));
  Decoder decoder_1 (.out0(code), .out1(data), .sel(cdm_8_mark5_1_p8), .en(mem));
  assign I_Odata = not_2_out ? cdm_8_mark5_1_p12 : 8'bz;  // Controlled_Buffer controlled_buffer_2
  not not_2 (not_2_out, In_out);
  // Probe on I_Oadr
  fixed_buffer fixed_buffer_1 (
    .update(clock), .row_0(write_buffer_1_row0), .row_1(write_buffer_1_row1), .row_2(write_buffer_1_row2),
    .row_3(write_buffer_1_row3), .row_4(write_buffer_1_row4), .row_5(write_buffer_1_row5),
    .row_6(write_buffer_1_row6), .row_7(write_buffer_1_row7), .row_8(write_buffer_1_row8),
    .row_9(write_buffer_1_row9), .row_10(write_buffer_1_row10), .row_11(write_buffer_1_row11),
    .row_12(write_buffer_1_row12), .row_13(write_buffer_1_row13), .row_14(write_buffer_1_row14),
    .row_15(write_buffer_1_row15), .row_16(write_buffer_1_row0_2), .row_17(write_buffer_1_row0_3),
    .row_18(write_buffer_1_row0_4), .row_19(write_buffer_1_row0_5), .row_20(write_buffer_1_row0_6),
    .row_21(write_buffer_1_row0_7), .row_22(write_buffer_1_row0_8), .row_23(write_buffer_1_row0_9),
    .row_24(write_buffer_1_row0_10), .row_25(write_buffer_1_row0_11), .row_26(write_buffer_1_row0_12),
    .row_27(write_buffer_1_row0_13), .row_28(write_buffer_1_row0_14), .row_29(write_buffer_1_row0_15),
    .row_30(write_buffer_1_row0_16), .row_31(write_buffer_1_row0_17), .row_0_2(fixed_buffer_1_row_0_2),
    .row_1_2(fixed_buffer_1_row_1_2), .row_2_2(fixed_buffer_1_row_2_2), .row_3_2(fixed_buffer_1_row_3_2),
    .row_4_2(fixed_buffer_1_row_4_2), .row_5_2(fixed_buffer_1_row_5_2), .row_6_2(fixed_buffer_1_row_6_2),
    .row_7_2(fixed_buffer_1_row_7_2), .row_8_2(fixed_buffer_1_row_8_2), .row_9_2(fixed_buffer_1_row_9_2),
    .row_10_2(fixed_buffer_1_row_10_2), .row_11_2(fixed_buffer_1_row_11_2),
    .row_12_2(fixed_buffer_1_row_12_2), .row_13_2(fixed_buffer_1_row_13_2),
    .row_14_2(fixed_buffer_1_row_14_2), .row_15_2(fixed_buffer_1_row_15_2),
    .row_16_2(fixed_buffer_1_row_16_2), .row_17_2(fixed_buffer_1_row_17_2),
    .row_18_2(fixed_buffer_1_row_18_2), .row_19_2(fixed_buffer_1_row_19_2),
    .row_20_2(fixed_buffer_1_row_20_2), .row_21_2(fixed_buffer_1_row_21_2),
    .row_22_2(fixed_buffer_1_row_22_2), .row_23_2(fixed_buffer_1_row_23_2),
    .row_24_2(fixed_buffer_1_row_24_2), .row_25_2(fixed_buffer_1_row_25_2),
    .row_26_2(fixed_buffer_1_row_26_2), .row_27_2(fixed_buffer_1_row_27_2),
    .row_28_2(fixed_buffer_1_row_28_2), .row_29_2(fixed_buffer_1_row_29_2),
    .row_30_2(fixed_buffer_1_row_30_2), .row_31_2(fixed_buffer_1_row_31_2));
  converter converter_1 (
    .row_0(write_buffer_1_row0), .row_1(write_buffer_1_row1), .row_2(write_buffer_1_row2),
    .row_3(write_buffer_1_row3), .row_4(write_buffer_1_row4), .row_5(write_buffer_1_row5),
    .row_6(write_buffer_1_row6), .row_7(write_buffer_1_row7), .row_8(write_buffer_1_row8),
    .row_9(write_buffer_1_row9), .row_10(write_buffer_1_row10), .row_11(write_buffer_1_row11),
    .row_12(write_buffer_1_row12), .row_13(write_buffer_1_row13), .row_14(write_buffer_1_row14),
    .row_15(write_buffer_1_row15), .row_16(write_buffer_1_row0_2), .row_17(write_buffer_1_row0_3),
    .row_18(write_buffer_1_row0_4), .row_19(write_buffer_1_row0_5), .row_20(write_buffer_1_row0_6),
    .row_21(write_buffer_1_row0_7), .row_22(write_buffer_1_row0_8), .row_23(write_buffer_1_row0_9),
    .row_24(write_buffer_1_row0_10), .row_25(write_buffer_1_row0_11), .row_26(write_buffer_1_row0_12),
    .row_27(write_buffer_1_row0_13), .row_28(write_buffer_1_row0_14), .row_29(write_buffer_1_row0_15),
    .row_30(write_buffer_1_row0_16), .row_31(write_buffer_1_row0_17),
    .converted_row(converter_1_converted_row), .Y(cursor_1_y), .X(cursor_1_x));
  // Debugger debugger_1: pin names not known
  cursor_visualization cursor_visualization_1 (
    .row_0(fixed_buffer_1_row_0_2), .row_1(fixed_buffer_1_row_1_2), .row_2(fixed_buffer_1_row_2_2),
    .row_3(fixed_buffer_1_row_3_2), .row_4(fixed_buffer_1_row_4_2), .row_5(fixed_buffer_1_row_5_2),
    .row_6(fixed_buffer_1_row_6_2), .row_7(fixed_buffer_1_row_7_2), .row_8(fixed_buffer_1_row_8_2),
    .row_9(fixed_buffer_1_row_9_2), .row_10(fixed_buffer_1_row_10_2), .row_11(fixed_buffer_1_row_11_2),
    .row_12(fixed_buffer_1_row_12_2), .row_13(fixed_buffer_1_row_13_2), .row_14(fixed_buffer_1_row_14_2),
    .row_15(fixed_buffer_1_row_15_2), .row_16(fixed_buffer_1_row_16_2), .row_17(fixed_buffer_1_row_17_2),
    .row_18(fixed_buffer_1_row_18_2), .row_19(fixed_buffer_1_row_19_2), .row_20(fixed_buffer_1_row_20_2),
    .row_21(fixed_buffer_1_row_21_2), .row_22(fixed_buffer_1_row_22_2), .row_23(fixed_buffer_1_row_23_2),
    .row_24(fixed_buffer_1_row_24_2), .row_25(fixed_buffer_1_row_25_2), .row_26(fixed_buffer_1_row_26_2),
    .row_27(fixed_buffer_1_row_27_2), .row_28(fixed_buffer_1_row_28_2), .row_29(fixed_buffer_1_row_29_2),
    .row_30(fixed_buffer_1_row_30_2), .row_31(fixed_buffer_1_row_31_2),
    .row_0_2(cursor_visualization_1_row_0_2), .row_1_2(cursor_visualization_1_row_1_2),
    .row_2_2(cursor_visualization_1_row_2_2), .row_3_2(cursor_visualization_1_row_3_2),
    .row_4_2(cursor_visualization_1_row_4_2), .row_5_2(cursor_visualization_1_row_5_2),
    .row_6_2(cursor_visualization_1_row_6_2), .row_7_2(cursor_visualization_1_row_7_2),
    .row_8_2(cursor_visualization_1_row_8_2), .row_9_2(cursor_visualization_1_row_9_2),
    .row_10_2(cursor_visualization_1_row_10_2), .row_11_2(cursor_visualization_1_row_11_2),
    .row_12_2(cursor_visualization_1_row_12_2), .row_13_2(cursor_visualization_1_row_13_2),
    .row_14_2(cursor_visualization_1_row_14_2), .row_15_2(cursor_visualization_1_row_15_2),
    .row_16_2(cursor_visualization_1_row_16_2), .row_17_2(cursor_visualization_1_row_17_2),
    .row_18_2(cursor_visualization_1_row_18_2), .row_19_2(cursor_visualization_1_row_19_2),
    .row_20_2(cursor_visualization_1_row_20_2), .row_21_2(cursor_visualization_1_row_21_2),
    .row_22_2(cursor_visualization_1_row_22_2), .row_23_2(cursor_visualization_1_row_23_2),
    .row_24_2(cursor_visualization_1_row_24_2), .row_25_2(cursor_visualization_1_row_25_2),
    .row_26_2(cursor_visualization_1_row_26_2), .row_27_2(cursor_visualization_1_row_27_2),
    .row_28_2(cursor_visualization_1_row_28_2), .row_29_2(cursor_visualization_1_row_29_2),
    .row_30_2(cursor_visualization_1_row_30_2), .row_31_2(cursor_visualization_1_row_31_2), .Y(cursor_1_y),
    .X(cursor_1_x), .on_off(on));
  ROM rom_1 (.addr(I_Oadr), .data(I_Odata), .sel(code));
  RAM ram_1 (.addr(I_Oadr), .data(I_Odata), .sel(RAM), .clk(clock), .ld(In_out));  // open: clr
  DotMatrix #(.inputtype("row"), .matrixcols(32), .matrixrows(32)) dotmatrix_1 (
    .row0(cursor_visualization_1_row_0_2), .row1(cursor_visualization_1_row_1_2),
    .row2(cursor_visualization_1_row_2_2), .row3(cursor_visualization_1_row_3_2),
    .row4(cursor_visualization_1_row_4_2), .row5(cursor_visualization_1_row_5_2),
    .row6(cursor_visualization_1_row_6_2), .row7(cursor_visualization_1_row_7_2),
    .row8(cursor_visualization_1_row_8_2), .row9(cursor_visualization_1_row_9_2),
    .row10(cursor_visualization_1_row_10_2), .row11(cursor_visualization_1_row_11_2),
    .row12(cursor_visualization_1_row_12_2), .row13(cursor_visualization_1_row_13_2),
    .row14(cursor_visualization_1_row_14_2), .row15(cursor_visualization_1_row_15_2),
    .row16(cursor_visualization_1_row_16_2), .row17(cursor_visualization_1_row_17_2),
    .row18(cursor_visualization_1_row_18_2), .row19(cursor_visualization_1_row_19_2),
    .row20(cursor_visualization_1_row_20_2), .row21(cursor_visualization_1_row_21_2),
    .row22(cursor_visualization_1_row_22_2), .row23(cursor_visualization_1_row_23_2),
    .row24(cursor_visualization_1_row_24_2), .row25(cursor_visualization_1_row_25_2),
    .row26(cursor_visualization_1_row_26_2), .row27(cursor_visualization_1_row_27_2),
    .row28(cursor_visualization_1_row_28_2), .row29(cursor_visualization_1_row_29_2),
    .row30(cursor_visualization_1_row_30_2), .row31(cursor_visualization_1_row_31_2));
  // Probe on I_Odata

  // Other names for the same wires on the sheet: rd_wr = In_out
endmodule

module write_buffer (
  input  clear,
  input  [31:0] \input ,
  input  write_not,
  input  [4:0] row,
  output [31:0] row0,
  output [31:0] row1,
  output [31:0] row2,
  output [31:0] row3,
  output [31:0] row4,
  output [31:0] row5,
  output [31:0] row6,
  output [31:0] row7,
  output [31:0] row8,
  output [31:0] row9,
  output [31:0] row10,
  output [31:0] row11,
  output [31:0] row12,
  output [31:0] row13,
  output [31:0] row14,
  output [31:0] row15,
  output [31:0] row0_2,
  output [31:0] row0_3,
  output [31:0] row0_4,
  output [31:0] row0_5,
  output [31:0] row0_6,
  output [31:0] row0_7,
  output [31:0] row0_8,
  output [31:0] row0_9,
  output [31:0] row0_10,
  output [31:0] row0_11,
  output [31:0] row0_12,
  output [31:0] row0_13,
  output [31:0] row0_14,
  output [31:0] row0_15,
  output [31:0] row0_16,
  output [31:0] row0_17
);

  wire decoder_1_out0, decoder_1_out1, decoder_1_out2, decoder_1_out3, decoder_1_out4, decoder_1_out5,
       decoder_1_out6, decoder_1_out7, decoder_1_out8, decoder_1_out9, decoder_1_out10, decoder_1_out11,
       decoder_1_out12, decoder_1_out13, decoder_1_out14, decoder_1_out15, decoder_1_out16, decoder_1_out17,
       decoder_1_out18, decoder_1_out19, decoder_1_out20, decoder_1_out21, decoder_1_out22, decoder_1_out23,
       decoder_1_out24, decoder_1_out25, decoder_1_out26, decoder_1_out27, decoder_1_out28, decoder_1_out29,
       decoder_1_out30, decoder_1_out31;

  Decoder #(.select(5), .disabled(0)) decoder_1 (
    .out0(decoder_1_out0), .out1(decoder_1_out1), .out2(decoder_1_out2), .out3(decoder_1_out3),
    .out4(decoder_1_out4), .out5(decoder_1_out5), .out6(decoder_1_out6), .out7(decoder_1_out7),
    .out8(decoder_1_out8), .out9(decoder_1_out9), .out10(decoder_1_out10), .out11(decoder_1_out11),
    .out12(decoder_1_out12), .out13(decoder_1_out13), .out14(decoder_1_out14), .out15(decoder_1_out15),
    .out16(decoder_1_out16), .out17(decoder_1_out17), .out18(decoder_1_out18), .out19(decoder_1_out19),
    .out20(decoder_1_out20), .out21(decoder_1_out21), .out22(decoder_1_out22), .out23(decoder_1_out23),
    .out24(decoder_1_out24), .out25(decoder_1_out25), .out26(decoder_1_out26), .out27(decoder_1_out27),
    .out28(decoder_1_out28), .out29(decoder_1_out29), .out30(decoder_1_out30), .out31(decoder_1_out31),
    .sel(row), .en(write_not));
  Register #(.width(32)) register_1 (.D(\input ), .Q(row0), .clk(decoder_1_out0), .clr(clear));  // open: en
  Register #(.width(32)) register_2 (.D(\input ), .Q(row1), .clk(decoder_1_out1), .clr(clear));  // open: en
  Register #(.width(32)) register_3 (.D(\input ), .Q(row2), .clk(decoder_1_out2), .clr(clear));  // open: en
  Register #(.width(32)) register_4 (.D(\input ), .Q(row3), .clk(decoder_1_out3), .clr(clear));  // open: en
  Register #(.width(32)) register_5 (.D(\input ), .Q(row4), .clk(decoder_1_out4), .clr(clear));  // open: en
  Register #(.width(32)) register_6 (.D(\input ), .Q(row5), .clk(decoder_1_out5), .clr(clear));  // open: en
  Register #(.width(32)) register_7 (.D(\input ), .Q(row6), .clk(decoder_1_out6), .clr(clear));  // open: en
  Register #(.width(32)) register_8 (.D(\input ), .Q(row7), .clk(decoder_1_out7), .clr(clear));  // open: en
  Register #(.width(32)) register_9 (.D(\input ), .Q(row8), .clk(decoder_1_out8), .clr(clear));  // open: en
  Register #(.width(32)) register_10 (.D(\input ), .Q(row9), .clk(decoder_1_out9), .clr(clear));  // open: en
  Register #(.width(32)) register_11 (.D(\input ), .Q(row10), .clk(decoder_1_out10), .clr(clear));  // open: en
  Register #(.width(32)) register_12 (.D(\input ), .Q(row11), .clk(decoder_1_out11), .clr(clear));  // open: en
  Register #(.width(32)) register_13 (.D(\input ), .Q(row12), .clk(decoder_1_out12), .clr(clear));  // open: en
  Register #(.width(32)) register_14 (.D(\input ), .Q(row13), .clk(decoder_1_out13), .clr(clear));  // open: en
  Register #(.width(32)) register_15 (.D(\input ), .Q(row14), .clk(decoder_1_out14), .clr(clear));  // open: en
  Register #(.width(32)) register_16 (.D(\input ), .Q(row15), .clk(decoder_1_out15), .clr(clear));  // open: en
  Register #(.width(32)) register_17 (.D(\input ), .Q(row0_2), .clk(decoder_1_out16), .clr(clear));  // open: en
  Register #(.width(32)) register_18 (.D(\input ), .Q(row0_3), .clk(decoder_1_out17), .clr(clear));  // open: en
  Register #(.width(32)) register_19 (.D(\input ), .Q(row0_4), .clk(decoder_1_out18), .clr(clear));  // open: en
  Register #(.width(32)) register_20 (.D(\input ), .Q(row0_5), .clk(decoder_1_out19), .clr(clear));  // open: en
  Register #(.width(32)) register_21 (.D(\input ), .Q(row0_6), .clk(decoder_1_out20), .clr(clear));  // open: en
  Register #(.width(32)) register_22 (.D(\input ), .Q(row0_7), .clk(decoder_1_out21), .clr(clear));  // open: en
  Register #(.width(32)) register_23 (.D(\input ), .Q(row0_8), .clk(decoder_1_out22), .clr(clear));  // open: en
  Register #(.width(32)) register_24 (.D(\input ), .Q(row0_9), .clk(decoder_1_out23), .clr(clear));  // open: en
  Register #(.width(32)) register_25 (.D(\input ), .Q(row0_10), .clk(decoder_1_out24), .clr(clear));  // open: en
  Register #(.width(32)) register_26 (.D(\input ), .Q(row0_11), .clk(decoder_1_out25), .clr(clear));  // open: en
  Register #(.width(32)) register_27 (.D(\input ), .Q(row0_12), .clk(decoder_1_out26), .clr(clear));  // open: en
  Register #(.width(32)) register_28 (.D(\input ), .Q(row0_13), .clk(decoder_1_out27), .clr(clear));  // open: en
  Register #(.width(32)) register_29 (.D(\input ), .Q(row0_14), .clk(decoder_1_out28), .clr(clear));  // open: en
  Register #(.width(32)) register_30 (.D(\input ), .Q(row0_15), .clk(decoder_1_out29), .clr(clear));  // open: en
  Register #(.width(32)) register_31 (.D(\input ), .Q(row0_16), .clk(decoder_1_out30), .clr(clear));  // open: en
  Register #(.width(32)) register_32 (.D(\input ), .Q(row0_17), .clk(decoder_1_out31), .clr(clear));  // open: en
endmodule

module converter (
  input  [31:0] row_0,
  input  [31:0] row_1,
  input  [31:0] row_2,
  input  [31:0] row_3,
  input  [31:0] row_4,
  input  [31:0] row_5,
  input  [31:0] row_6,
  input  [31:0] row_7,
  input  [31:0] row_8,
  input  [31:0] row_9,
  input  [31:0] row_10,
  input  [31:0] row_11,
  input  [4:0] Y,
  input  [4:0] X,
  input  [31:0] row_12,
  input  [31:0] row_13,
  input  [31:0] row_14,
  input  [31:0] row_15,
  input  [31:0] row_16,
  input  [31:0] row_17,
  input  [31:0] row_18,
  input  [31:0] row_19,
  input  [31:0] row_20,
  input  [31:0] row_21,
  input  [31:0] row_22,
  input  [31:0] row_23,
  input  [31:0] row_24,
  input  [31:0] row_25,
  input  [31:0] row_26,
  input  [31:0] row_27,
  input  [31:0] row_28,
  input  [31:0] row_29,
  input  [31:0] row_30,
  input  [31:0] row_31,
  output [31:0] converted_row
);

  wire [31:0] decoder_1_out0, multiplexer_1_out;

  Multiplexer #(.select(5), .width(32), .disabled(0), .enable("false")) multiplexer_1 (
    .in0(row_0), .in1(row_1), .in2(row_2), .in3(row_3), .in4(row_4), .in5(row_5), .in6(row_6), .in7(row_7),
    .in8(row_8), .in9(row_9), .in10(row_10), .in11(row_11), .in12(row_12), .in13(row_13), .in14(row_14),
    .in15(row_15), .in16(row_16), .in17(row_17), .in18(row_18), .in19(row_19), .in20(row_20), .in21(row_21),
    .in22(row_22), .in23(row_23), .in24(row_24), .in25(row_25), .in26(row_26), .in27(row_27), .in28(row_28),
    .in29(row_29), .in30(row_30), .in31(row_31), .out(multiplexer_1_out), .sel(Y));
  Decoder #(.select(5), .disabled(0), .enable("false")) decoder_1 (
    .out0(decoder_1_out0[0]), .out1(decoder_1_out0[1]), .out2(decoder_1_out0[2]), .out3(decoder_1_out0[3]),
    .out4(decoder_1_out0[4]), .out5(decoder_1_out0[5]), .out6(decoder_1_out0[6]), .out7(decoder_1_out0[7]),
    .out8(decoder_1_out0[8]), .out9(decoder_1_out0[9]), .out10(decoder_1_out0[10]),
    .out11(decoder_1_out0[11]), .out12(decoder_1_out0[12]), .out13(decoder_1_out0[13]),
    .out14(decoder_1_out0[14]), .out15(decoder_1_out0[15]), .out16(decoder_1_out0[16]),
    .out17(decoder_1_out0[17]), .out18(decoder_1_out0[18]), .out19(decoder_1_out0[19]),
    .out20(decoder_1_out0[20]), .out21(decoder_1_out0[21]), .out22(decoder_1_out0[22]),
    .out23(decoder_1_out0[23]), .out24(decoder_1_out0[24]), .out25(decoder_1_out0[25]),
    .out26(decoder_1_out0[26]), .out27(decoder_1_out0[27]), .out28(decoder_1_out0[28]),
    .out29(decoder_1_out0[29]), .out30(decoder_1_out0[30]), .out31(decoder_1_out0[31]), .sel(X));
  assign converted_row = decoder_1_out0 ^ multiplexer_1_out;  // XOR_Gate xor_1, 32 bits wide
endmodule

module fixed_buffer (
  input  update,
  input  [31:0] row_0,
  input  [31:0] row_1,
  input  [31:0] row_2,
  input  [31:0] row_3,
  input  [31:0] row_4,
  input  [31:0] row_5,
  input  [31:0] row_6,
  input  [31:0] row_7,
  input  [31:0] row_8,
  input  [31:0] row_9,
  input  [31:0] row_10,
  input  [31:0] row_11,
  input  [31:0] row_12,
  input  [31:0] row_13,
  input  [31:0] row_14,
  input  [31:0] row_15,
  input  [31:0] row_16,
  input  [31:0] row_17,
  input  [31:0] row_18,
  input  [31:0] row_19,
  input  [31:0] row_20,
  input  [31:0] row_21,
  input  [31:0] row_22,
  input  [31:0] row_23,
  input  [31:0] row_24,
  input  [31:0] row_25,
  input  [31:0] row_26,
  input  [31:0] row_27,
  input  [31:0] row_28,
  input  [31:0] row_29,
  input  [31:0] row_30,
  input  [31:0] row_31,
  output [31:0] row_0_2,
  output [31:0] row_1_2,
  output [31:0] row_2_2,
  output [31:0] row_3_2,
  output [31:0] row_4_2,
  output [31:0] row_5_2,
  output [31:0] row_6_2,
  output [31:0] row_7_2,
  output [31:0] row_8_2,
  output [31:0] row_9_2,
  output [31:0] row_10_2,
  output [31:0] row_11_2,
  output [31:0] row_12_2,
  output [31:0] row_13_2,
  output [31:0] row_14_2,
  output [31:0] row_15_2,
  output [31:0] row_16_2,
  output [31:0] row_17_2,
  output [31:0] row_18_2,
  output [31:0] row_19_2,
  output [31:0] row_20_2,
  output [31:0] row_21_2,
  output [31:0] row_22_2,
  output [31:0] row_23_2,
  output [31:0] row_24_2,
  output [31:0] row_25_2,
  output [31:0] row_26_2,
  output [31:0] row_27_2,
  output [31:0] row_28_2,
  output [31:0] row_29_2,
  output [31:0] row_30_2,
  output [31:0] row_31_2
);

  Register #(.width(32)) register_1 (.D(row_0), .Q(row_0_2), .clk(update));  // open: en, clr
  Register #(.width(32)) register_2 (.D(row_1), .Q(row_1_2), .clk(update));  // open: en, clr
  Register #(.width(32)) register_3 (.D(row_2), .Q(row_2_2), .clk(update));  // open: en, clr
  Register #(.width(32)) register_4 (.D(row_3), .Q(row_3_2), .clk(update));  // open: en, clr
  Register #(.width(32)) register_5 (.D(row_4), .Q(row_4_2), .clk(update));  // open: en, clr
  Register #(.width(32)) register_6 (.D(row_5), .Q(row_5_2), .clk(update));  // open: en, clr
  Register #(.width(32)) register_7 (.D(row_6), .Q(row_6_2), .clk(update));  // open: en, clr
  Register #(.width(32)) register_8 (.D(row_7), .Q(row_7_2), .clk(update));  // open: en, clr
  Register #(.width(32)) register_9 (.D(row_8), .Q(row_8_2), .clk(update));  // open: en, clr
  Register #(.width(32)) register_10 (.D(row_9), .Q(row_9_2), .clk(update));  // open: en, clr
  Register #(.width(32)) register_11 (.D(row_10), .Q(row_10_2), .clk(update));  // open: en, clr
  Register #(.width(32)) register_12 (.D(row_11), .Q(row_11_2), .clk(update));  // open: en, clr
  Register #(.width(32)) register_13 (.D(row_12), .Q(row_12_2), .clk(update));  // open: en, clr
  Register #(.width(32)) register_14 (.D(row_13), .Q(row_13_2), .clk(update));  // open: en, clr
  Register #(.width(32)) register_15 (.D(row_14), .Q(row_14_2), .clk(update));  // open: en, clr
  Register #(.width(32)) register_16 (.D(row_15), .Q(row_15_2), .clk(update));  // open: en, clr
  Register #(.width(32)) register_17 (.D(row_16), .Q(row_16_2), .clk(update));  // open: en, clr
  Register #(.width(32)) register_18 (.D(row_17), .Q(row_17_2), .clk(update));  // open: en, clr
  Register #(.width(32)) register_19 (.D(row_18), .Q(row_18_2), .clk(update));  // open: en, clr
  Register #(.width(32)) register_20 (.D(row_19), .Q(row_19_2), .clk(update));  // open: en, clr
  Register #(.width(32)) register_21 (.D(row_20), .Q(row_20_2), .clk(update));  // open: en, clr
  Register #(.width(32)) register_22 (.D(row_21), .Q(row_21_2), .clk(update));  // open: en, clr
  Register #(.width(32)) register_23 (.D(row_22), .Q(row_22_2), .clk(update));  // open: en, clr
  Register #(.width(32)) register_24 (.D(row_23), .Q(row_23_2), .clk(update));  // open: en, clr
  Register #(.width(32)) register_25 (.D(row_24), .Q(row_24_2), .clk(update));  // open: en, clr
  Register #(.width(32)) register_26 (.D(row_25), .Q(row_25_2), .clk(update));  // open: en, clr
  Register #(.width(32)) register_27 (.D(row_26), .Q(row_26_2), .clk(update));  // open: en, clr
  Register #(.width(32)) register_28 (.D(row_27), .Q(row_27_2), .clk(update));  // open: en, clr
  Register #(.width(32)) register_29 (.D(row_28), .Q(row_28_2), .clk(update));  // open: en, clr
  Register #(.width(32)) register_30 (.D(row_29), .Q(row_29_2), .clk(update));  // open: en, clr
  Register #(.width(32)) register_31 (.D(row_30), .Q(row_30_2), .clk(update));  // open: en, clr
  Register #(.width(32)) register_32 (.D(row_31), .Q(row_31_2), .clk(update));  // open: en, clr
endmodule

module calculator (
  input  [31:0] row_0,
  input  [4:0] X,
  input  [4:0] Y,
  input  [31:0] row_1,
  input  [31:0] row_2,
  input  [31:0] row_3,
  input  [31:0] row_4,
  input  [31:0] row_5,
  input  [31:0] row_6,
  input  [31:0] row_7,
  input  [31:0] row_8,
  input  [31:0] row_9,
  input  [31:0] row_10,
  input  [31:0] row_11,
  input  [31:0] row_12,
  input  [31:0] row_13,
  input  [31:0] row_14,
  input  [31:0] row_15,
  input  [31:0] row_16,
  input  [31:0] row_17,
  input  [31:0] row_18,
  input  [31:0] row_19,
  input  [31:0] row_20,
  input  [31:0] row_21,
  input  [31:0] row_22,
  input  [31:0] row_23,
  input  [31:0] row_24,
  input  [31:0] row_25,
  input  [31:0] row_26,
  input  [31:0] row_27,
  input  [31:0] row_28,
  input  [31:0] row_29,
  input  [31:0] row_30,
  input  [31:0] row_31
);

  wire [4:0] adder_1_out, subtractor_1_out;
  wire [31:0] multiplexer_1_out, multiplexer_2_out, multiplexer_3_out;

  Subtractor #(.width(5)) subtractor_1 (.a(Y), .b(5'b00001), .out(subtractor_1_out));  // open: bin, bout
  Multiplexer #(.select(5), .width(32), .disabled(0), .enable("false")) multiplexer_1 (
    .in0(row_0), .in1(row_1), .in2(row_2), .in3(row_3), .in4(row_4), .in5(row_5), .in6(row_6), .in7(row_7),
    .in8(row_8), .in9(row_9), .in10(row_10), .in11(row_11), .in12(row_12), .in13(row_13), .in14(row_14),
    .in15(row_15), .in16(row_16), .in17(row_17), .in18(row_18), .in19(row_19), .in20(row_20), .in21(row_21),
    .in22(row_22), .in23(row_23), .in24(row_24), .in25(row_25), .in26(row_26), .in27(row_27), .in28(row_28),
    .in29(row_29), .in30(row_30), .in31(row_31), .out(multiplexer_1_out), .sel(subtractor_1_out));
  Multiplexer #(.select(5), .width(32), .disabled(0), .enable("false")) multiplexer_2 (
    .in0(row_0), .in1(row_1), .in2(row_2), .in3(row_3), .in4(row_4), .in5(row_5), .in6(row_6), .in7(row_7),
    .in8(row_8), .in9(row_9), .in10(row_10), .in11(row_11), .in12(row_12), .in13(row_13), .in14(row_14),
    .in15(row_15), .in16(row_16), .in17(row_17), .in18(row_18), .in19(row_19), .in20(row_20), .in21(row_21),
    .in22(row_22), .in23(row_23), .in24(row_24), .in25(row_25), .in26(row_26), .in27(row_27), .in28(row_28),
    .in29(row_29), .in30(row_30), .in31(row_31), .out(multiplexer_2_out), .sel(Y));
  Adder #(.width(5)) adder_1 (.a(Y), .b(5'b00001), .out(adder_1_out));  // open: cin, cout
  Multiplexer #(.select(5), .width(32), .disabled(0), .enable("false")) multiplexer_3 (
    .in0(row_0), .in1(row_1), .in2(row_2), .in3(row_3), .in4(row_4), .in5(row_5), .in6(row_6), .in7(row_7),
    .in8(row_8), .in9(row_9), .in10(row_10), .in11(row_11), .in12(row_12), .in13(row_13), .in14(row_14),
    .in15(row_15), .in16(row_16), .in17(row_17), .in18(row_18), .in19(row_19), .in20(row_20), .in21(row_21),
    .in22(row_22), .in23(row_23), .in24(row_24), .in25(row_25), .in26(row_26), .in27(row_27), .in28(row_28),
    .in29(row_29), .in30(row_30), .in31(row_31), .out(multiplexer_3_out), .sel(adder_1_out));

  // Other names for the same wires on the sheet: row0[31:0] = row_0; row1[31:0] = row_1; row2[31:0] = row_2;
  //   row3[31:0] = row_3; row4[31:0] = row_4; row5[31:0] = row_5; row6[31:0] = row_6; row7[31:0] = row_7;
  //   row8[31:0] = row_8; row9[31:0] = row_9; row10[31:0] = row_10; row11[31:0] = row_11; row12[31:0] = row_12;
  //   row13[31:0] = row_13; row14[31:0] = row_14; row15[31:0] = row_15; row16[31:0] = row_16; row17[31:0] = row_17;
  //   row18[31:0] = row_18; row19[31:0] = row_19; row20[31:0] = row_20; row21[31:0] = row_21; row22[31:0] = row_22;
  //   row23[31:0] = row_23; row24[31:0] = row_24; row25[31:0] = row_25; row26[31:0] = row_26; row27[31:0] = row_27;
  //   row28[31:0] = row_28; row29[31:0] = row_29; row30[31:0] = row_30; row31[31:0] = row_31

  // Notes on the sheet:
  //   UP
  //   MIDDLE
  //   DOWN
endmodule

module cursor (
  input  [6:0] ASCII_code,
  output [4:0] X,
  output [4:0] Y,
  output is_enter
);

  wire comparator_1_eq, comparator_2_eq, comparator_3_eq, comparator_4_eq, or_1_out, or_2_out;
  wire [6:0] adder_1_out, adder_2_out, subtractor_1_out, subtractor_2_out, transistor_1_out, transistor_2_out;
  wire [6:5] X_out, Y_out;

  // Probe on ASCII_code
  Comparator #(.width(7)) comparator_1 (.a(ASCII_code), .b(7'b1100100), .eq(comparator_1_eq));  // open: gt, lt
  Comparator #(.width(7)) comparator_2 (.a(ASCII_code), .b(7'b1100001), .eq(comparator_2_eq));  // open: gt, lt
  Comparator #(.width(7)) comparator_3 (.a(ASCII_code), .b(7'b1110111), .eq(comparator_3_eq));  // open: gt, lt
  Comparator #(.width(7)) comparator_4 (.a(ASCII_code), .b(7'b1110011), .eq(comparator_4_eq));  // open: gt, lt
  Comparator #(.width(7)) comparator_5 (.a(ASCII_code), .b(7'b1100101), .eq(is_enter));  // open: gt, lt
  Adder #(.width(7)) adder_1 (.a(7'b0000001), .b({X_out, X}), .out(adder_1_out));  // open: cin, cout
  Subtractor #(.width(7)) subtractor_1 (.a({X_out, X}), .b(7'b0000001), .out(subtractor_1_out));  // open: bin, bout
  Adder #(.width(7)) adder_2 (.a(7'b0000001), .b({Y_out, Y}), .out(adder_2_out));  // open: cin, cout
  Subtractor #(.width(7)) subtractor_2 (.a({Y_out, Y}), .b(7'b0000001), .out(subtractor_2_out));  // open: bin, bout
  Transistor #(.\type ("n"), .width(7)) transistor_1 (
    .in(subtractor_1_out), .out(transistor_1_out), .gate(comparator_1_eq));
  Transistor #(.\type ("n"), .gate("br"), .width(7)) transistor_2 (
    .in(adder_2_out), .out(transistor_2_out), .gate(comparator_4_eq));
  or or_1 (or_1_out, comparator_1_eq, comparator_2_eq);
  Transistor #(.width(7)) transistor_3 (.in(adder_1_out), .out(transistor_1_out), .gate(comparator_1_eq));
  Transistor #(.gate("br"), .width(7)) transistor_4 (
    .in(subtractor_2_out), .out(transistor_2_out), .gate(comparator_4_eq));
  or or_2 (or_2_out, comparator_3_eq, comparator_4_eq);
  Register #(.width(7)) u_X (.D(transistor_1_out), .Q({X_out, X}), .clk(or_1_out));  // open: en, clr
  Register #(.width(7)) u_Y (.D(transistor_2_out), .Q({Y_out, Y}), .clk(or_2_out));  // open: en, clr

  // Other names for the same wires on the sheet: X_out[4:0] = X; Y_out[4:0] = Y

  // Notes on the sheet:
  //   =D
  //   =A
  //   =W
  //   =S
endmodule

module cursor_visualization (
  input  [31:0] row_0,
  input  [31:0] row_1,
  input  [31:0] row_2,
  input  [31:0] row_3,
  input  [31:0] row_4,
  input  [31:0] row_5,
  input  [31:0] row_6,
  input  [31:0] row_7,
  input  [31:0] row_8,
  input  [31:0] row_9,
  input  [4:0] Y,
  input  on_off,
  input  [4:0] X,
  input  [31:0] row_10,
  input  [31:0] row_11,
  input  [31:0] row_12,
  input  [31:0] row_13,
  input  [31:0] row_14,
  input  [31:0] row_15,
  input  [31:0] row_16,
  input  [31:0] row_17,
  input  [31:0] row_18,
  input  [31:0] row_19,
  input  [31:0] row_20,
  input  [31:0] row_21,
  input  [31:0] row_22,
  input  [31:0] row_23,
  input  [31:0] row_24,
  input  [31:0] row_25,
  input  [31:0] row_26,
  input  [31:0] row_27,
  input  [31:0] row_28,
  input  [31:0] row_29,
  input  [31:0] row_30,
  input  [31:0] row_31,
  output [31:0] row_0_2,
  output [31:0] row_1_2,
  output [31:0] row_2_2,
  output [31:0] row_3_2,
  output [31:0] row_4_2,
  output [31:0] row_5_2,
  output [31:0] row_6_2,
  output [31:0] row_7_2,
  output [31:0] row_8_2,
  output [31:0] row_9_2,
  output [31:0] row_10_2,
  output [31:0] row_11_2,
  output [31:0] row_12_2,
  output [31:0] row_13_2,
  output [31:0] row_14_2,
  output [31:0] row_15_2,
  output [31:0] row_16_2,
  output [31:0] row_17_2,
  output [31:0] row_18_2,
  output [31:0] row_19_2,
  output [31:0] row_20_2,
  output [31:0] row_21_2,
  output [31:0] row_22_2,
  output [31:0] row_23_2,
  output [31:0] row_24_2,
  output [31:0] row_25_2,
  output [31:0] row_26_2,
  output [31:0] row_27_2,
  output [31:0] row_28_2,
  output [31:0] row_29_2,
  output [31:0] row_30_2,
  output [31:0] row_31_2
);

  wire comparator_1_eq, comparator_2_eq, comparator_3_eq, comparator_4_eq, comparator_5_eq, comparator_6_eq,
       comparator_7_eq, comparator_8_eq, comparator_9_eq, comparator_10_eq, comparator_11_eq,
       comparator_12_eq, comparator_13_eq, comparator_14_eq, comparator_15_eq, comparator_16_eq,
       comparator_17_eq, comparator_18_eq, comparator_19_eq, comparator_20_eq, comparator_21_eq,
       comparator_22_eq, comparator_23_eq, comparator_24_eq, comparator_25_eq, comparator_26_eq,
       comparator_27_eq, comparator_28_eq, comparator_29_eq, comparator_30_eq, comparator_31_eq,
       comparator_32_eq, pull_resistor_1_node, pull_resistor_2_node, pull_resistor_5_node,
       pull_resistor_8_node, pull_resistor_9_node, pull_resistor_12_node, pull_resistor_13_node,
       pull_resistor_14_node, pull_resistor_17_node, pull_resistor_20_node, pull_resistor_22_node,
       pull_resistor_23_node, pull_resistor_24_node, pull_resistor_26_node, pull_resistor_27_node,
       pull_resistor_28_node, pull_resistor_30_node, pull_resistor_31_node, transistor_3_out,
       transistor_4_out, transistor_6_out, transistor_7_out, transistor_10_out, transistor_11_out,
       transistor_15_out, transistor_16_out, transistor_18_out, transistor_19_out, transistor_21_out,
       transistor_25_out, transistor_29_out, transistor_32_out;
  wire [31:0] decoder_1_out0, multiplexer_1_out, new_row;

  Multiplexer #(.select(5), .width(32), .disabled(0), .enable("false")) multiplexer_1 (
    .in0(row_0), .in1(row_1), .in2(row_2), .in3(row_3), .in4(row_4), .in5(row_5), .in6(row_6), .in7(row_7),
    .in8(row_8), .in9(row_9), .in10(row_10), .in11(row_11), .in12(row_12), .in13(row_13), .in14(row_14),
    .in15(row_15), .in16(row_16), .in17(row_17), .in18(row_18), .in19(row_19), .in20(row_20), .in21(row_21),
    .in22(row_22), .in23(row_23), .in24(row_24), .in25(row_25), .in26(row_26), .in27(row_27), .in28(row_28),
    .in29(row_29), .in30(row_30), .in31(row_31), .out(multiplexer_1_out), .sel(Y));
  Decoder #(.select(5), .disabled(0), .enable("false")) decoder_1 (
    .out0(decoder_1_out0[0]), .out1(decoder_1_out0[1]), .out2(decoder_1_out0[2]), .out3(decoder_1_out0[3]),
    .out4(decoder_1_out0[4]), .out5(decoder_1_out0[5]), .out6(decoder_1_out0[6]), .out7(decoder_1_out0[7]),
    .out8(decoder_1_out0[8]), .out9(decoder_1_out0[9]), .out10(decoder_1_out0[10]),
    .out11(decoder_1_out0[11]), .out12(decoder_1_out0[12]), .out13(decoder_1_out0[13]),
    .out14(decoder_1_out0[14]), .out15(decoder_1_out0[15]), .out16(decoder_1_out0[16]),
    .out17(decoder_1_out0[17]), .out18(decoder_1_out0[18]), .out19(decoder_1_out0[19]),
    .out20(decoder_1_out0[20]), .out21(decoder_1_out0[21]), .out22(decoder_1_out0[22]),
    .out23(decoder_1_out0[23]), .out24(decoder_1_out0[24]), .out25(decoder_1_out0[25]),
    .out26(decoder_1_out0[26]), .out27(decoder_1_out0[27]), .out28(decoder_1_out0[28]),
    .out29(decoder_1_out0[29]), .out30(decoder_1_out0[30]), .out31(decoder_1_out0[31]), .sel(X));
  assign new_row = decoder_1_out0 | multiplexer_1_out;  // OR_Gate or_1, 32 bits wide
  Comparator #(.width(5)) comparator_1 (.a({5{1'b0}}), .b(Y), .eq(comparator_1_eq));  // open: gt, lt
  Comparator #(.width(5)) comparator_2 (.a(5'b00001), .b(Y), .eq(comparator_2_eq));  // open: gt, lt
  Comparator #(.width(5)) comparator_3 (.a(5'b00010), .b(Y), .eq(comparator_3_eq));  // open: gt, lt
  Comparator #(.width(5)) comparator_4 (.a(5'b00011), .b(Y), .eq(comparator_4_eq));  // open: gt, lt
  Comparator #(.width(5)) comparator_5 (.a(5'b00100), .b(Y), .eq(comparator_5_eq));  // open: gt, lt
  Comparator #(.width(5)) comparator_6 (.a(5'b00101), .b(Y), .eq(comparator_6_eq));  // open: gt, lt
  Comparator #(.width(5)) comparator_7 (.a(5'b00110), .b(Y), .eq(comparator_7_eq));  // open: gt, lt
  Comparator #(.width(5)) comparator_8 (.a(5'b00111), .b(Y), .eq(comparator_8_eq));  // open: gt, lt
  Comparator #(.width(5)) comparator_9 (.a(5'b01000), .b(Y), .eq(comparator_9_eq));  // open: gt, lt
  Comparator #(.width(5)) comparator_10 (.a(5'b01001), .b(Y), .eq(comparator_10_eq));  // open: gt, lt
  Comparator #(.width(5)) comparator_11 (.a(5'b01010), .b(Y), .eq(comparator_11_eq));  // open: gt, lt
  Comparator #(.width(5)) comparator_12 (.a(5'b01011), .b(Y), .eq(comparator_12_eq));  // open: gt, lt
  Comparator #(.width(5)) comparator_13 (.a(5'b01100), .b(Y), .eq(comparator_13_eq));  // open: gt, lt
  Comparator #(.width(5)) comparator_14 (.a(5'b01101), .b(Y), .eq(comparator_14_eq));  // open: gt, lt
  Comparator #(.width(5)) comparator_15 (.a(5'b01110), .b(Y), .eq(comparator_15_eq));  // open: gt, lt
  Comparator #(.width(5)) comparator_16 (.a(5'b01111), .b(Y), .eq(comparator_16_eq));  // open: gt, lt
  Comparator #(.width(5)) comparator_17 (.a(5'b10000), .b(Y), .eq(comparator_17_eq));  // open: gt, lt
  Comparator #(.width(5)) comparator_18 (.a(5'b10001), .b(Y), .eq(comparator_18_eq));  // open: gt, lt
  Comparator #(.width(5)) comparator_19 (.a(5'b10010), .b(Y), .eq(comparator_19_eq));  // open: gt, lt
  Comparator #(.width(5)) comparator_20 (.a(5'b10011), .b(Y), .eq(comparator_20_eq));  // open: gt, lt
  Comparator #(.width(5)) comparator_21 (.a(5'b10100), .b(Y), .eq(comparator_21_eq));  // open: gt, lt
  Comparator #(.width(5)) comparator_22 (.a(5'b10101), .b(Y), .eq(comparator_22_eq));  // open: gt, lt
  Comparator #(.width(5)) comparator_23 (.a(5'b10110), .b(Y), .eq(comparator_23_eq));  // open: gt, lt
  Comparator #(.width(5)) comparator_24 (.a(5'b10111), .b(Y), .eq(comparator_24_eq));  // open: gt, lt
  Comparator #(.width(5)) comparator_25 (.a(5'b11000), .b(Y), .eq(comparator_25_eq));  // open: gt, lt
  Comparator #(.width(5)) comparator_26 (.a(5'b11001), .b(Y), .eq(comparator_26_eq));  // open: gt, lt
  Comparator #(.width(5)) comparator_27 (.a(5'b11010), .b(Y), .eq(comparator_27_eq));  // open: gt, lt
  Comparator #(.width(5)) comparator_28 (.a(5'b11011), .b(Y), .eq(comparator_28_eq));  // open: gt, lt
  Comparator #(.width(5)) comparator_29 (.a(5'b11100), .b(Y), .eq(comparator_29_eq));  // open: gt, lt
  Comparator #(.width(5)) comparator_30 (.a(5'b11101), .b(Y), .eq(comparator_30_eq));  // open: gt, lt
  Comparator #(.width(5)) comparator_31 (.a(5'b11110), .b(Y), .eq(comparator_31_eq));  // open: gt, lt
  Comparator #(.width(5)) comparator_32 (.a({5{1'b1}}), .b(Y), .eq(comparator_32_eq));  // open: gt, lt
  Pull_Resistor pull_resistor_1 (.node(pull_resistor_1_node));
  Transistor transistor_1 (.in(comparator_1_eq), .out(pull_resistor_1_node), .gate(on_off));
  Multiplexer #(.width(32), .disabled(0), .enable("false")) multiplexer_2 (
    .in0(row_0), .in1(new_row), .out(row_0_2), .sel(pull_resistor_1_node));
  Pull_Resistor pull_resistor_2 (.node(pull_resistor_2_node));
  Transistor transistor_2 (.in(comparator_2_eq), .out(pull_resistor_2_node), .gate(on_off));
  Multiplexer #(.width(32), .disabled(0), .enable("false")) multiplexer_3 (
    .in0(row_1), .in1(new_row), .out(row_1_2), .sel(pull_resistor_2_node));
  Transistor transistor_3 (.in(comparator_3_eq), .out(transistor_3_out), .gate(on_off));
  Pull_Resistor pull_resistor_3 (.node(transistor_3_out));
  Multiplexer #(.width(32), .disabled(0), .enable("false")) multiplexer_4 (
    .in0(row_2), .in1(new_row), .out(row_2_2), .sel(transistor_3_out));
  Transistor transistor_4 (.in(comparator_4_eq), .out(transistor_4_out), .gate(on_off));
  Pull_Resistor pull_resistor_4 (.node(transistor_4_out));
  Multiplexer #(.width(32), .disabled(0), .enable("false")) multiplexer_5 (
    .in0(row_3), .in1(new_row), .out(row_3_2), .sel(transistor_4_out));
  Pull_Resistor pull_resistor_5 (.node(pull_resistor_5_node));
  Transistor transistor_5 (.in(comparator_5_eq), .out(pull_resistor_5_node), .gate(on_off));
  Multiplexer #(.width(32), .disabled(0), .enable("false")) multiplexer_6 (
    .in0(row_4), .in1(new_row), .out(row_4_2), .sel(pull_resistor_5_node));
  Transistor transistor_6 (.in(comparator_6_eq), .out(transistor_6_out), .gate(on_off));
  Pull_Resistor pull_resistor_6 (.node(transistor_6_out));
  Multiplexer #(.width(32), .disabled(0), .enable("false")) multiplexer_7 (
    .in0(row_5), .in1(new_row), .out(row_5_2), .sel(transistor_6_out));
  Transistor transistor_7 (.in(comparator_7_eq), .out(transistor_7_out), .gate(on_off));
  Pull_Resistor pull_resistor_7 (.node(transistor_7_out));
  Multiplexer #(.width(32), .disabled(0), .enable("false")) multiplexer_8 (
    .in0(row_6), .in1(new_row), .out(row_6_2), .sel(transistor_7_out));
  Pull_Resistor pull_resistor_8 (.node(pull_resistor_8_node));
  Transistor transistor_8 (.in(comparator_8_eq), .out(pull_resistor_8_node), .gate(on_off));
  Multiplexer #(.width(32), .disabled(0), .enable("false")) multiplexer_9 (
    .in0(row_7), .in1(new_row), .out(row_7_2), .sel(pull_resistor_8_node));
  Pull_Resistor pull_resistor_9 (.node(pull_resistor_9_node));
  Transistor transistor_9 (.in(comparator_9_eq), .out(pull_resistor_9_node), .gate(on_off));
  Multiplexer #(.width(32), .disabled(0), .enable("false")) multiplexer_10 (
    .in0(row_8), .in1(new_row), .out(row_8_2), .sel(pull_resistor_9_node));
  Transistor transistor_10 (.in(comparator_10_eq), .out(transistor_10_out), .gate(on_off));
  Pull_Resistor pull_resistor_10 (.node(transistor_10_out));
  Multiplexer #(.width(32), .disabled(0), .enable("false")) multiplexer_11 (
    .in0(row_9), .in1(new_row), .out(row_9_2), .sel(transistor_10_out));
  Transistor transistor_11 (.in(comparator_11_eq), .out(transistor_11_out), .gate(on_off));
  Pull_Resistor pull_resistor_11 (.node(transistor_11_out));
  Multiplexer #(.width(32), .disabled(0), .enable("false")) multiplexer_12 (
    .in0(row_10), .in1(new_row), .out(row_10_2), .sel(transistor_11_out));
  Pull_Resistor pull_resistor_12 (.node(pull_resistor_12_node));
  Transistor transistor_12 (.in(comparator_12_eq), .out(pull_resistor_12_node), .gate(on_off));
  Multiplexer #(.width(32), .disabled(0), .enable("false")) multiplexer_13 (
    .in0(row_11), .in1(new_row), .out(row_11_2), .sel(pull_resistor_12_node));
  Pull_Resistor pull_resistor_13 (.node(pull_resistor_13_node));
  Transistor transistor_13 (.in(comparator_13_eq), .out(pull_resistor_13_node), .gate(on_off));
  Multiplexer #(.width(32), .disabled(0), .enable("false")) multiplexer_14 (
    .in0(row_12), .in1(new_row), .out(row_12_2), .sel(pull_resistor_13_node));
  Pull_Resistor pull_resistor_14 (.node(pull_resistor_14_node));
  Transistor transistor_14 (.in(comparator_14_eq), .out(pull_resistor_14_node), .gate(on_off));
  Multiplexer #(.width(32), .disabled(0), .enable("false")) multiplexer_15 (
    .in0(row_13), .in1(new_row), .out(row_13_2), .sel(pull_resistor_14_node));
  Transistor transistor_15 (.in(comparator_15_eq), .out(transistor_15_out), .gate(on_off));
  Pull_Resistor pull_resistor_15 (.node(transistor_15_out));
  Multiplexer #(.width(32), .disabled(0), .enable("false")) multiplexer_16 (
    .in0(row_14), .in1(new_row), .out(row_14_2), .sel(transistor_15_out));
  Transistor transistor_16 (.in(comparator_16_eq), .out(transistor_16_out), .gate(on_off));
  Pull_Resistor pull_resistor_16 (.node(transistor_16_out));
  Multiplexer #(.width(32), .disabled(0), .enable("false")) multiplexer_17 (
    .in0(row_15), .in1(new_row), .out(row_15_2), .sel(transistor_16_out));
  Pull_Resistor pull_resistor_17 (.node(pull_resistor_17_node));
  Transistor transistor_17 (.in(comparator_17_eq), .out(pull_resistor_17_node), .gate(on_off));
  Multiplexer #(.width(32), .disabled(0), .enable("false")) multiplexer_18 (
    .in0(row_16), .in1(new_row), .out(row_16_2), .sel(pull_resistor_17_node));
  Transistor transistor_18 (.in(comparator_18_eq), .out(transistor_18_out), .gate(on_off));
  Pull_Resistor pull_resistor_18 (.node(transistor_18_out));
  Multiplexer #(.width(32), .disabled(0), .enable("false")) multiplexer_19 (
    .in0(row_17), .in1(new_row), .out(row_17_2), .sel(transistor_18_out));
  Transistor transistor_19 (.in(comparator_19_eq), .out(transistor_19_out), .gate(on_off));
  Pull_Resistor pull_resistor_19 (.node(transistor_19_out));
  Multiplexer #(.width(32), .disabled(0), .enable("false")) multiplexer_20 (
    .in0(row_18), .in1(new_row), .out(row_18_2), .sel(transistor_19_out));
  Pull_Resistor pull_resistor_20 (.node(pull_resistor_20_node));
  Transistor transistor_20 (.in(comparator_20_eq), .out(pull_resistor_20_node), .gate(on_off));
  Multiplexer #(.width(32), .disabled(0), .enable("false")) multiplexer_21 (
    .in0(row_19), .in1(new_row), .out(row_19_2), .sel(pull_resistor_20_node));
  Transistor transistor_21 (.in(comparator_21_eq), .out(transistor_21_out), .gate(on_off));
  Pull_Resistor pull_resistor_21 (.node(transistor_21_out));
  Multiplexer #(.width(32), .disabled(0), .enable("false")) multiplexer_22 (
    .in0(row_20), .in1(new_row), .out(row_20_2), .sel(transistor_21_out));
  Pull_Resistor pull_resistor_22 (.node(pull_resistor_22_node));
  Transistor transistor_22 (.in(comparator_22_eq), .out(pull_resistor_22_node), .gate(on_off));
  Multiplexer #(.width(32), .disabled(0), .enable("false")) multiplexer_23 (
    .in0(row_21), .in1(new_row), .out(row_21_2), .sel(pull_resistor_22_node));
  Pull_Resistor pull_resistor_23 (.node(pull_resistor_23_node));
  Transistor transistor_23 (.in(comparator_23_eq), .out(pull_resistor_23_node), .gate(on_off));
  Multiplexer #(.width(32), .disabled(0), .enable("false")) multiplexer_24 (
    .in0(row_22), .in1(new_row), .out(row_22_2), .sel(pull_resistor_23_node));
  Pull_Resistor pull_resistor_24 (.node(pull_resistor_24_node));
  Transistor transistor_24 (.in(comparator_24_eq), .out(pull_resistor_24_node), .gate(on_off));
  Multiplexer #(.width(32), .disabled(0), .enable("false")) multiplexer_25 (
    .in0(row_23), .in1(new_row), .out(row_23_2), .sel(pull_resistor_24_node));
  Transistor transistor_25 (.in(comparator_25_eq), .out(transistor_25_out), .gate(on_off));
  Pull_Resistor pull_resistor_25 (.node(transistor_25_out));
  Multiplexer #(.width(32), .disabled(0), .enable("false")) multiplexer_26 (
    .in0(row_24), .in1(new_row), .out(row_24_2), .sel(transistor_25_out));
  Pull_Resistor pull_resistor_26 (.node(pull_resistor_26_node));
  Transistor transistor_26 (.in(comparator_26_eq), .out(pull_resistor_26_node), .gate(on_off));
  Multiplexer #(.width(32), .disabled(0), .enable("false")) multiplexer_27 (
    .in0(row_25), .in1(new_row), .out(row_25_2), .sel(pull_resistor_26_node));
  Pull_Resistor pull_resistor_27 (.node(pull_resistor_27_node));
  Transistor transistor_27 (.in(comparator_27_eq), .out(pull_resistor_27_node), .gate(on_off));
  Multiplexer #(.width(32), .disabled(0), .enable("false")) multiplexer_28 (
    .in0(row_26), .in1(new_row), .out(row_26_2), .sel(pull_resistor_27_node));
  Pull_Resistor pull_resistor_28 (.node(pull_resistor_28_node));
  Transistor transistor_28 (.in(comparator_28_eq), .out(pull_resistor_28_node), .gate(on_off));
  Multiplexer #(.width(32), .disabled(0), .enable("false")) multiplexer_29 (
    .in0(row_27), .in1(new_row), .out(row_27_2), .sel(pull_resistor_28_node));
  Transistor transistor_29 (.in(comparator_29_eq), .out(transistor_29_out), .gate(on_off));
  Pull_Resistor pull_resistor_29 (.node(transistor_29_out));
  Multiplexer #(.width(32), .disabled(0), .enable("false")) multiplexer_30 (
    .in0(row_28), .in1(new_row), .out(row_28_2), .sel(transistor_29_out));
  Pull_Resistor pull_resistor_30 (.node(pull_resistor_30_node));
  Transistor transistor_30 (.in(comparator_30_eq), .out(pull_resistor_30_node), .gate(on_off));
  Multiplexer #(.width(32), .disabled(0), .enable("false")) multiplexer_31 (
    .in0(row_29), .in1(new_row), .out(row_29_2), .sel(pull_resistor_30_node));
  Pull_Resistor pull_resistor_31 (.node(pull_resistor_31_node));
  Transistor transistor_31 (.in(comparator_31_eq), .out(pull_resistor_31_node), .gate(on_off));
  Multiplexer #(.width(32), .disabled(0), .enable("false")) multiplexer_32 (
    .in0(row_30), .in1(new_row), .out(row_30_2), .sel(pull_resistor_31_node));
  Transistor transistor_32 (.in(comparator_32_eq), .out(transistor_32_out), .gate(on_off));
  Pull_Resistor pull_resistor_32 (.node(transistor_32_out));
  Multiplexer #(.width(32), .disabled(0), .enable("false")) multiplexer_33 (
    .in0(row_31), .in1(new_row), .out(row_31_2), .sel(transistor_32_out));

  // Other names for the same wires on the sheet: _0[31:0] = row_0; _1[31:0] = row_1; _2[31:0] = row_2;
  //   _3[31:0] = row_3; _4[31:0] = row_4; _5[31:0] = row_5; _6[31:0] = row_6; _7[31:0] = row_7; _8[31:0] = row_8;
  //   _9[31:0] = row_9; _10[31:0] = row_10; _11[31:0] = row_11; _12[31:0] = row_12; _13[31:0] = row_13;
  //   _14[31:0] = row_14; _15[31:0] = row_15; _16[31:0] = row_16; _17[31:0] = row_17; _18[31:0] = row_18;
  //   _19[31:0] = row_19; _20[31:0] = row_20; _21[31:0] = row_21; _22[31:0] = row_22; _23[31:0] = row_23;
  //   _24[31:0] = row_24; _25[31:0] = row_25; _26[31:0] = row_26; _27[31:0] = row_27; _28[31:0] = row_28;
  //   _29[31:0] = row_29; _30[31:0] = row_30; _31[31:0] = row_31; on = on_off
endmodule
