// Logisim project test.circ as structural Verilog: 1 circuit, main circuit main
module main (
);

  wire cdm_8_mark5_1_p1, cdm_8_mark5_1_p2, cdm_8_mark5_1_p4, cdm_8_mark5_1_p5, clock, code, data, mem,
       not_1_out, rd_wr;
  wire [7:0] cdm_8_mark5_1_p8, cdm_8_mark5_1_p9, cdm_8_mark5_1_p10, controlled_buffer_1_out;

  // Probe on cdm_8_mark5_1_p1
  // Probe on cdm_8_mark5_1_p2
  // Probe on cdm_8_mark5_1_p4
  // Probe on nothing
  Clock clock_1 (.out(clock));
  // CdM_8_mark5 cdm_8_mark5_1: pin names not known; wires that end beside it: cdm_8_mark5_1_p1, cdm_8_mark5_1_p2, clock, cdm_8_mark5_1_p4, cdm_8_mark5_1_p5, mem, rd_wr, cdm_8_mark5_1_p8, cdm_8_mark5_1_p9, cdm_8_mark5_1_p10
  Pull_Resistor pull_resistor_1 (.node(code));
  Pull_Resistor pull_resistor_2 (.node(data));
  Decoder decoder_1 (.out0(code), .out1(data), .sel(cdm_8_mark5_1_p5), .en(mem));
  assign controlled_buffer_1_out = not_1_out ? cdm_8_mark5_1_p9 : 8'bz;  // Controlled_Buffer controlled_buffer_1
  not not_1 (not_1_out, rd_wr);
  assign cdm_8_mark5_1_p10 = rd_wr ? controlled_buffer_1_out : 8'bz;  // Controlled_Buffer controlled_buffer_2
  // Debugger debugger_1: pin names not known
  ROM rom_1 (.addr(cdm_8_mark5_1_p8), .data(controlled_buffer_1_out), .sel(code));
  RAM ram_1 (
    .addr(cdm_8_mark5_1_p8), .data(controlled_buffer_1_out), .sel(data), .clk(clock), .ld(rd_wr));  // open: clr
  // Probe on controlled_buffer_1_out

  // Notes on the sheet:
  //   contents of rom_1 (hex, n*v repeats v):
  //   d0 4 f1 d4 61 63 68 61 72 73 6
endmodule
